// Logisim project dao54_lab5.circ as structural Verilog: 1 circuit, main circuit main
module main (
  input  [3:0] A,
  input  [3:0] B,
  input  sub
);

  wire adder_1_cout, and_1_out, and_2_out, not_2_out, not_3_out, not_4_out, SOV, UOV;
  wire [3:0] _0, multiplexer_1_out, not_1_p2;

  // NOT_Gate #(.width(4)) not_1: pin names not known; wires that end beside it: B, not_1_p2
  Multiplexer #(.width(4)) multiplexer_1 (.in0(B), .in1(not_1_p2), .out(multiplexer_1_out), .sel(sub));  // open: en
  // Probe on A
  // Probe on B
  // Probe on _0
  LED led_1 (.in(UOV));
  Adder #(.width(4)) adder_1 (.a(A), .b(multiplexer_1_out), .out(_0), .cin(sub), .cout(adder_1_cout));
  xor xor_1 (UOV, adder_1_cout, sub);
  // Probe on A
  // Probe on B
  // Probe on _0
  LED led_2 (.in(SOV));
  not not_2 (not_2_out, A[3]);
  not not_3 (not_3_out, _0[3]);
  // NOT_Gate not_4 has open pins: in=open, out=not_4_out
  and and_1 (and_1_out, multiplexer_1_out[3], not_3_out, A[3]);
  and and_2 (and_2_out, not_2_out, _0[3], not_4_out);
  or or_1 (SOV, and_1_out, and_2_out);
endmodule
